# Fritzing sketch ambientsensorstation (saved by Fritzing 0.9.4)
circuit board: 4.4cm x 4cm
breadboards: 1

parts:
  Switch = Pushbutton [package=THT]
  BME280 = GY-BMEP280 Barometric Pressure Sensor - Breakout
  CCS811 = Adafruit CCS811
  NodeMCU = ESP8266 NodeMCU LoLin module
  GY-2561 = GY-2561 clone sensor from TSL2561

nets:
  N1: Switch.leg0, NodeMCU.D3
  GND: Switch.leg1, BME280.GND, CCS811.GND, CCS811.!WAKE, NodeMCU.GND, GY-2561.GND
  N2: BME280.SDO, NodeMCU.D7
  N3: BME280.CSB, NodeMCU.D6
  N4: BME280.SDA, NodeMCU.D8
  N5: BME280.SCL, NodeMCU.D5
  VCC: BME280.VCC, CCS811.VIN, NodeMCU.3V3, GY-2561.VCC
  N6: CCS811.SDA, NodeMCU.D2, GY-2561.SDA
  N7: CCS811.SCL, NodeMCU.D1, GY-2561.SCL
  N8: NodeMCU.D0, NodeMCU.RST

notes:
  ambient
  v1.0
  Lolin

custom parts:
  GY-BMEP280 Barometric Pressure Sensor - Breakout: The BME280 is a chip which was originally designed for the next generation of smartphones. It is made up of a very accurate pressure sensor and an associated temperature sensor which helps calibrate the pressure readings. And just for fun they threw in a pretty solid humidity sensor in there as well! So with an I2C connection you have access to enough weather data to make some pretty good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
  ESP8266 NodeMCU LoLin module: ESP8266 based NodeMCU
